// Logisim project 32-1-Bit-Multiplier.circ as structural Verilog: 1 circuit, main circuit 32-1-Bit-Multiplier
module _32_1_Bit_Multiplier (
  input  [31:0] A,
  input  B,
  output [31:0] OM
);

  Multiplexer #(.width(32), .enable("false")) multiplexer_1 (.in0({32{1'b0}}), .in1(A), .out(OM), .sel(B));
endmodule
