// Logisim project 32-Bit-ALU.circ as structural Verilog: 1 circuit, main circuit main
module main (
  input  [31:0] A,
  input  [31:0] B,
  input  [5:0] OPCODE,
  output [31:0] C,
  output Zero,
  output Carryout,
  output Overflow
);

  wire ADD_C, ADD_O, MULT_C, SUB_C, SUB_O, xor_1_out, xor_2_out, xor_3_out, xor_4_out;
  wire [0:0] SLT;
  wire [31:0] ADD, AND, HIGH_MULT, MULT, not_1_out, OR, SLL, SRA, SRL, SUB, XOR;

  xor xor_1 (xor_1_out, A[31], ADD[31]);
  and and_1 (ADD_O, xor_1_out, xor_2_out);
  xor xor_2 (xor_2_out, B[31], ADD[31]);
  xor xor_3 (xor_3_out, A[31], SUB[31]);
  and and_2 (SUB_O, xor_3_out, xor_4_out);
  xor xor_4 (xor_4_out, B[31], SUB[31]);
  assign not_1_out = ~B;  // NOT_Gate not_1, 32 bits wide
  not not_2 (SLT[0], SUB_C);
  _32_BIT_ADDER u_32_bit_adder_1 (.A(A), .CarryIn0(1'b1), .B(not_1_out), .SUM(SUB), .CarryOut(SUB_C));
  _32_BIT_ADDER u_32_bit_adder_2 (.A(A), .CarryIn0(1'b0), .B(B), .SUM(ADD), .CarryOut(ADD_C));
  assign AND = A & B;  // AND_Gate and_3, 32 bits wide
  assign OR = A | B;  // OR_Gate or_1, 32 bits wide
  Multiplexer #(.select(4), .enable("false")) multiplexer_1 (
    .in0(SUB_C), .in1(ADD_C), .in2(MULT_C), .in3(1'b0), .in4(1'b0), .in5(1'b0), .in6(1'b0), .in7(1'b0),
    .in8(1'b0), .in9(1'b0), .out(Carryout), .sel(OPCODE[3:0]));  // open: in10, in11, in12, in13, in14, in15
  Multiplexer #(.select(4), .enable("false")) multiplexer_2 (
    .in0(SUB_O), .in1(ADD_O), .in2(1'b1), .in3(1'b0), .in4(1'b0), .in5(1'b0), .in6(1'b0), .in7(1'b0),
    .in8(1'b0), .in9(1'b0), .out(Overflow), .sel(OPCODE[3:0]));  // open: in10, in11, in12, in13, in14, in15
  assign XOR = A ^ B;  // XOR_Gate xor_5, 32 bits wide
  Multiplexer #(.select(4), .width(32), .enable("false")) multiplexer_3 (
    .in0(SUB), .in1(ADD), .in2(MULT), .in3(AND), .in4(OR), .in5(XOR), .in6(SLL), .in7({{31{1'b0}}, SLT[0]}),
    .in8(SRA), .in9(SRL), .out(C), .sel(OPCODE[3:0]));  // open: in10, in11, in12, in13, in14, in15
  EqZero eqzero_1 (.A(SUB), .out_2(Zero));
  Shift_Right_Local shift_right_local_1 (.A(A), .S(B[4:0]), .LL_SHIFTED(SRL));
  Shift_Left_Logical shift_left_logical_1 (.A(A), .S(B[4:0]), .LL_SHIFTED(SLL));
  _32_Bit_MULT MULTIP (.Multiplicand(A), .Multiplier(B), .HIGH(HIGH_MULT), .LOW(MULT));
  Shift_Right_Arithmetic shift_right_arithmetic_1 (.A(A), .S(B[4:0]), .LL_SHIFTED(SRA));

  // Other names for the same wires on the sheet: B5[4:0] = B[4:0]; SELECT[3:0] = OPCODE[3:0]
endmodule
