// Logisim project 32-Bit-AdvancedMultiplier.circ as structural Verilog: 1 circuit, main circuit 32-Bit-AdvancedMultiplier
module _32_Bit_AdvancedMultiplier (
  input  [31:0] A,
  input  [31:0] B,
  output [31:0] C
);

  wire [31:0] n32_1_bit_multiplier_1_om, n32_1_bit_multiplier_2_om, n32_1_bit_multiplier_3_om,
       n32_1_bit_multiplier_4_om, n32_1_bit_multiplier_5_om, n32_1_bit_multiplier_6_om,
       n32_1_bit_multiplier_7_om, n32_1_bit_multiplier_8_om, n32_1_bit_multiplier_9_om,
       n32_1_bit_multiplier_10_om, n32_1_bit_multiplier_11_om, n32_1_bit_multiplier_12_om,
       n32_1_bit_multiplier_13_om, n32_1_bit_multiplier_14_om, n32_1_bit_multiplier_15_om,
       n32_1_bit_multiplier_16_om, n32_1_bit_multiplier_17_om, n32_1_bit_multiplier_18_om,
       n32_1_bit_multiplier_19_om, n32_1_bit_multiplier_20_om, n32_1_bit_multiplier_21_om,
       n32_1_bit_multiplier_22_om, n32_1_bit_multiplier_23_om, n32_1_bit_multiplier_24_om,
       n32_1_bit_multiplier_25_om, n32_1_bit_multiplier_26_om, n32_1_bit_multiplier_27_om,
       n32_1_bit_multiplier_28_om, n32_1_bit_multiplier_29_om, n32_1_bit_multiplier_30_om,
       n32_1_bit_multiplier_31_om, n32_1_bit_multiplier_32_om, n32_bit_adder_1_sum, n32_bit_adder_2_sum,
       n32_bit_adder_3_sum, n32_bit_adder_4_sum, n32_bit_adder_5_sum, n32_bit_adder_6_sum,
       n32_bit_adder_7_sum, n32_bit_adder_8_sum, n32_bit_adder_9_sum, n32_bit_adder_10_sum,
       n32_bit_adder_11_sum, n32_bit_adder_12_sum, n32_bit_adder_13_sum, n32_bit_adder_14_sum,
       n32_bit_adder_15_sum, n32_bit_adder_16_sum, n32_bit_adder_17_sum, n32_bit_adder_18_sum,
       n32_bit_adder_19_sum, n32_bit_adder_20_sum, n32_bit_adder_21_sum, n32_bit_adder_22_sum,
       n32_bit_adder_23_sum, n32_bit_adder_24_sum, n32_bit_adder_25_sum, n32_bit_adder_26_sum,
       n32_bit_adder_27_sum, n32_bit_adder_28_sum, n32_bit_adder_29_sum, n32_bit_adder_30_sum,
       shift_left_logical_1_ll_shifted, shift_left_logical_2_ll_shifted, shift_left_logical_3_ll_shifted,
       shift_left_logical_4_ll_shifted, shift_left_logical_5_ll_shifted, shift_left_logical_6_ll_shifted,
       shift_left_logical_7_ll_shifted, shift_left_logical_8_ll_shifted, shift_left_logical_9_ll_shifted,
       shift_left_logical_10_ll_shifted, shift_left_logical_11_ll_shifted, shift_left_logical_12_ll_shifted,
       shift_left_logical_13_ll_shifted, shift_left_logical_14_ll_shifted, shift_left_logical_15_ll_shifted,
       shift_left_logical_16_ll_shifted, shift_left_logical_17_ll_shifted, shift_left_logical_18_ll_shifted,
       shift_left_logical_19_ll_shifted, shift_left_logical_20_ll_shifted, shift_left_logical_21_ll_shifted,
       shift_left_logical_22_ll_shifted, shift_left_logical_23_ll_shifted, shift_left_logical_24_ll_shifted,
       shift_left_logical_25_ll_shifted, shift_left_logical_26_ll_shifted, shift_left_logical_27_ll_shifted,
       shift_left_logical_28_ll_shifted, shift_left_logical_29_ll_shifted, shift_left_logical_30_ll_shifted,
       shift_left_logical_31_ll_shifted;

  // Probe on C
  _32_1_Bit_Multiplier u_32_1_bit_multiplier_1 (.A(A), .B(B[31]), .OM(n32_1_bit_multiplier_1_om));
  Shift_Left_Logical shift_left_logical_1 (
    .A(n32_1_bit_multiplier_1_om), .S({5{1'b1}}), .LL_SHIFTED(shift_left_logical_1_ll_shifted));
  _32_1_Bit_Multiplier u_32_1_bit_multiplier_2 (.A(A), .B(B[30]), .OM(n32_1_bit_multiplier_2_om));
  Shift_Left_Logical shift_left_logical_2 (
    .A(n32_1_bit_multiplier_2_om), .S(5'b11110), .LL_SHIFTED(shift_left_logical_2_ll_shifted));
  Shift_Left_Logical shift_left_logical_3 (
    .A(n32_1_bit_multiplier_4_om), .S(5'b11101), .LL_SHIFTED(shift_left_logical_3_ll_shifted));
  _32_BIT_ADDER u_32_bit_adder_1 (
    .A(shift_left_logical_2_ll_shifted), .CarryIn0(1'b0), .B(shift_left_logical_1_ll_shifted),
    .SUM(n32_bit_adder_1_sum));  // open: CarryOut
  _32_1_Bit_Multiplier u_32_1_bit_multiplier_3 (.A(A), .B(B[28]), .OM(n32_1_bit_multiplier_3_om));
  _32_1_Bit_Multiplier u_32_1_bit_multiplier_4 (.A(A), .B(B[29]), .OM(n32_1_bit_multiplier_4_om));
  Shift_Left_Logical shift_left_logical_4 (
    .A(n32_1_bit_multiplier_3_om), .S(5'b11100), .LL_SHIFTED(shift_left_logical_4_ll_shifted));
  _32_BIT_ADDER u_32_bit_adder_2 (
    .A(shift_left_logical_4_ll_shifted), .CarryIn0(1'b0), .B(shift_left_logical_3_ll_shifted),
    .SUM(n32_bit_adder_2_sum));  // open: CarryOut
  _32_BIT_ADDER u_32_bit_adder_3 (
    .A(n32_bit_adder_2_sum), .CarryIn0(1'b0), .B(n32_bit_adder_1_sum), .SUM(n32_bit_adder_3_sum));  // open: CarryOut
  _32_1_Bit_Multiplier u_32_1_bit_multiplier_5 (.A(A), .B(B[26]), .OM(n32_1_bit_multiplier_5_om));
  _32_1_Bit_Multiplier u_32_1_bit_multiplier_6 (.A(A), .B(B[27]), .OM(n32_1_bit_multiplier_6_om));
  Shift_Left_Logical shift_left_logical_5 (
    .A(n32_1_bit_multiplier_6_om), .S(5'b11011), .LL_SHIFTED(shift_left_logical_5_ll_shifted));
  Shift_Left_Logical shift_left_logical_6 (
    .A(n32_1_bit_multiplier_5_om), .S(5'b11010), .LL_SHIFTED(shift_left_logical_6_ll_shifted));
  _32_BIT_ADDER u_32_bit_adder_4 (
    .A(shift_left_logical_6_ll_shifted), .CarryIn0(1'b0), .B(shift_left_logical_5_ll_shifted),
    .SUM(n32_bit_adder_4_sum));  // open: CarryOut
  _32_1_Bit_Multiplier u_32_1_bit_multiplier_7 (.A(A), .B(B[25]), .OM(n32_1_bit_multiplier_7_om));
  Shift_Left_Logical shift_left_logical_7 (
    .A(n32_1_bit_multiplier_9_om), .S(5'b11000), .LL_SHIFTED(shift_left_logical_7_ll_shifted));
  Shift_Left_Logical shift_left_logical_8 (
    .A(n32_1_bit_multiplier_7_om), .S(5'b11001), .LL_SHIFTED(shift_left_logical_8_ll_shifted));
  _32_1_Bit_Multiplier u_32_1_bit_multiplier_8 (.A(A), .B(B[23]), .OM(n32_1_bit_multiplier_8_om));
  _32_1_Bit_Multiplier u_32_1_bit_multiplier_9 (.A(A), .B(B[24]), .OM(n32_1_bit_multiplier_9_om));
  Shift_Left_Logical shift_left_logical_9 (
    .A(n32_1_bit_multiplier_8_om), .S(5'b10111), .LL_SHIFTED(shift_left_logical_9_ll_shifted));
  _32_BIT_ADDER u_32_bit_adder_5 (
    .A(shift_left_logical_7_ll_shifted), .CarryIn0(1'b0), .B(shift_left_logical_8_ll_shifted),
    .SUM(n32_bit_adder_5_sum));  // open: CarryOut
  _32_BIT_ADDER u_32_bit_adder_6 (
    .A(n32_bit_adder_5_sum), .CarryIn0(1'b0), .B(n32_bit_adder_4_sum), .SUM(n32_bit_adder_6_sum));  // open: CarryOut
  _32_BIT_ADDER u_32_bit_adder_7 (
    .A(n32_bit_adder_6_sum), .CarryIn0(1'b0), .B(n32_bit_adder_3_sum), .SUM(n32_bit_adder_7_sum));  // open: CarryOut
  _32_1_Bit_Multiplier u_32_1_bit_multiplier_10 (.A(A), .B(B[22]), .OM(n32_1_bit_multiplier_10_om));
  Shift_Left_Logical shift_left_logical_10 (
    .A(n32_1_bit_multiplier_12_om), .S(5'b10101), .LL_SHIFTED(shift_left_logical_10_ll_shifted));
  Shift_Left_Logical shift_left_logical_11 (
    .A(n32_1_bit_multiplier_10_om), .S(5'b10110), .LL_SHIFTED(shift_left_logical_11_ll_shifted));
  _32_BIT_ADDER u_32_bit_adder_8 (
    .A(shift_left_logical_11_ll_shifted), .CarryIn0(1'b0), .B(shift_left_logical_9_ll_shifted),
    .SUM(n32_bit_adder_8_sum));  // open: CarryOut
  _32_1_Bit_Multiplier u_32_1_bit_multiplier_11 (.A(A), .B(B[20]), .OM(n32_1_bit_multiplier_11_om));
  _32_1_Bit_Multiplier u_32_1_bit_multiplier_12 (.A(A), .B(B[21]), .OM(n32_1_bit_multiplier_12_om));
  Shift_Left_Logical shift_left_logical_12 (
    .A(n32_1_bit_multiplier_11_om), .S(5'b10100), .LL_SHIFTED(shift_left_logical_12_ll_shifted));
  _32_BIT_ADDER u_32_bit_adder_9 (
    .A(shift_left_logical_12_ll_shifted), .CarryIn0(1'b0), .B(shift_left_logical_10_ll_shifted),
    .SUM(n32_bit_adder_9_sum));  // open: CarryOut
  _32_BIT_ADDER u_32_bit_adder_10 (
    .A(n32_bit_adder_9_sum), .CarryIn0(1'b0), .B(n32_bit_adder_8_sum), .SUM(n32_bit_adder_10_sum));  // open: CarryOut
  _32_1_Bit_Multiplier u_32_1_bit_multiplier_13 (.A(A), .B(B[18]), .OM(n32_1_bit_multiplier_13_om));
  _32_1_Bit_Multiplier u_32_1_bit_multiplier_14 (.A(A), .B(B[19]), .OM(n32_1_bit_multiplier_14_om));
  Shift_Left_Logical shift_left_logical_13 (
    .A(n32_1_bit_multiplier_14_om), .S(5'b10011), .LL_SHIFTED(shift_left_logical_13_ll_shifted));
  Shift_Left_Logical shift_left_logical_14 (
    .A(n32_1_bit_multiplier_13_om), .S(5'b10010), .LL_SHIFTED(shift_left_logical_14_ll_shifted));
  _32_BIT_ADDER u_32_bit_adder_11 (
    .A(shift_left_logical_14_ll_shifted), .CarryIn0(1'b0), .B(shift_left_logical_13_ll_shifted),
    .SUM(n32_bit_adder_11_sum));  // open: CarryOut
  _32_1_Bit_Multiplier u_32_1_bit_multiplier_15 (.A(A), .B(B[17]), .OM(n32_1_bit_multiplier_15_om));
  Shift_Left_Logical shift_left_logical_15 (
    .A(n32_1_bit_multiplier_15_om), .S(5'b10001), .LL_SHIFTED(shift_left_logical_15_ll_shifted));
  Shift_Left_Logical shift_left_logical_16 (
    .A(n32_1_bit_multiplier_17_om), .S(5'b10000), .LL_SHIFTED(shift_left_logical_16_ll_shifted));
  _32_BIT_ADDER u_32_bit_adder_12 (
    .A(shift_left_logical_16_ll_shifted), .CarryIn0(1'b0), .B(shift_left_logical_15_ll_shifted),
    .SUM(n32_bit_adder_12_sum));  // open: CarryOut
  _32_BIT_ADDER u_32_bit_adder_13 (
    .A(n32_bit_adder_12_sum), .CarryIn0(1'b0), .B(n32_bit_adder_11_sum), .SUM(n32_bit_adder_13_sum));  // open: CarryOut
  _32_BIT_ADDER u_32_bit_adder_14 (
    .A(n32_bit_adder_13_sum), .CarryIn0(1'b0), .B(n32_bit_adder_10_sum), .SUM(n32_bit_adder_14_sum));  // open: CarryOut
  _32_BIT_ADDER u_32_bit_adder_15 (
    .A(n32_bit_adder_14_sum), .CarryIn0(1'b0), .B(n32_bit_adder_7_sum), .SUM(n32_bit_adder_15_sum));  // open: CarryOut
  _32_1_Bit_Multiplier u_32_1_bit_multiplier_16 (.A(A), .B(B[15]), .OM(n32_1_bit_multiplier_16_om));
  _32_1_Bit_Multiplier u_32_1_bit_multiplier_17 (.A(A), .B(B[16]), .OM(n32_1_bit_multiplier_17_om));
  Shift_Left_Logical shift_left_logical_17 (
    .A(n32_1_bit_multiplier_16_om), .S(5'b01111), .LL_SHIFTED(shift_left_logical_17_ll_shifted));
  _32_1_Bit_Multiplier u_32_1_bit_multiplier_18 (.A(A), .B(B[14]), .OM(n32_1_bit_multiplier_18_om));
  Shift_Left_Logical shift_left_logical_18 (
    .A(n32_1_bit_multiplier_18_om), .S(5'b01110), .LL_SHIFTED(shift_left_logical_18_ll_shifted));
  Shift_Left_Logical shift_left_logical_19 (
    .A(n32_1_bit_multiplier_20_om), .S(5'b01101), .LL_SHIFTED(shift_left_logical_19_ll_shifted));
  _32_BIT_ADDER u_32_bit_adder_16 (
    .A(shift_left_logical_18_ll_shifted), .CarryIn0(1'b0), .B(shift_left_logical_17_ll_shifted),
    .SUM(n32_bit_adder_16_sum));  // open: CarryOut
  _32_1_Bit_Multiplier u_32_1_bit_multiplier_19 (.A(A), .B(B[12]), .OM(n32_1_bit_multiplier_19_om));
  _32_1_Bit_Multiplier u_32_1_bit_multiplier_20 (.A(A), .B(B[13]), .OM(n32_1_bit_multiplier_20_om));
  Shift_Left_Logical shift_left_logical_20 (
    .A(n32_1_bit_multiplier_19_om), .S(5'b01100), .LL_SHIFTED(shift_left_logical_20_ll_shifted));
  _32_BIT_ADDER u_32_bit_adder_17 (
    .A(shift_left_logical_20_ll_shifted), .CarryIn0(1'b0), .B(shift_left_logical_19_ll_shifted),
    .SUM(n32_bit_adder_17_sum));  // open: CarryOut
  _32_BIT_ADDER u_32_bit_adder_18 (
    .A(n32_bit_adder_17_sum), .CarryIn0(1'b0), .B(n32_bit_adder_16_sum), .SUM(n32_bit_adder_18_sum));  // open: CarryOut
  _32_1_Bit_Multiplier u_32_1_bit_multiplier_21 (.A(A), .B(B[10]), .OM(n32_1_bit_multiplier_21_om));
  _32_1_Bit_Multiplier u_32_1_bit_multiplier_22 (.A(A), .B(B[11]), .OM(n32_1_bit_multiplier_22_om));
  Shift_Left_Logical shift_left_logical_21 (
    .A(n32_1_bit_multiplier_22_om), .S(5'b01011), .LL_SHIFTED(shift_left_logical_21_ll_shifted));
  Shift_Left_Logical shift_left_logical_22 (
    .A(n32_1_bit_multiplier_21_om), .S(5'b01010), .LL_SHIFTED(shift_left_logical_22_ll_shifted));
  _32_BIT_ADDER u_32_bit_adder_19 (
    .A(shift_left_logical_22_ll_shifted), .CarryIn0(1'b0), .B(shift_left_logical_21_ll_shifted),
    .SUM(n32_bit_adder_19_sum));  // open: CarryOut
  _32_1_Bit_Multiplier u_32_1_bit_multiplier_23 (.A(A), .B(B[9]), .OM(n32_1_bit_multiplier_23_om));
  Shift_Left_Logical shift_left_logical_23 (
    .A(n32_1_bit_multiplier_25_om), .S(5'b01000), .LL_SHIFTED(shift_left_logical_23_ll_shifted));
  Shift_Left_Logical shift_left_logical_24 (
    .A(n32_1_bit_multiplier_23_om), .S(5'b01001), .LL_SHIFTED(shift_left_logical_24_ll_shifted));
  _32_BIT_ADDER u_32_bit_adder_20 (
    .A(shift_left_logical_23_ll_shifted), .CarryIn0(1'b0), .B(shift_left_logical_24_ll_shifted),
    .SUM(n32_bit_adder_20_sum));  // open: CarryOut
  _32_BIT_ADDER u_32_bit_adder_21 (
    .A(n32_bit_adder_20_sum), .CarryIn0(1'b0), .B(n32_bit_adder_19_sum), .SUM(n32_bit_adder_21_sum));  // open: CarryOut
  _32_BIT_ADDER u_32_bit_adder_22 (
    .A(n32_bit_adder_21_sum), .CarryIn0(1'b0), .B(n32_bit_adder_18_sum), .SUM(n32_bit_adder_22_sum));  // open: CarryOut
  _32_1_Bit_Multiplier u_32_1_bit_multiplier_24 (.A(A), .B(B[7]), .OM(n32_1_bit_multiplier_24_om));
  _32_1_Bit_Multiplier u_32_1_bit_multiplier_25 (.A(A), .B(B[8]), .OM(n32_1_bit_multiplier_25_om));
  Shift_Left_Logical shift_left_logical_25 (
    .A(n32_1_bit_multiplier_24_om), .S(5'b00111), .LL_SHIFTED(shift_left_logical_25_ll_shifted));
  _32_1_Bit_Multiplier u_32_1_bit_multiplier_26 (.A(A), .B(B[6]), .OM(n32_1_bit_multiplier_26_om));
  Shift_Left_Logical shift_left_logical_26 (
    .A(n32_1_bit_multiplier_28_om), .S(5'b00101), .LL_SHIFTED(shift_left_logical_26_ll_shifted));
  Shift_Left_Logical shift_left_logical_27 (
    .A(n32_1_bit_multiplier_26_om), .S(5'b00110), .LL_SHIFTED(shift_left_logical_27_ll_shifted));
  _32_BIT_ADDER u_32_bit_adder_23 (
    .A(shift_left_logical_27_ll_shifted), .CarryIn0(1'b0), .B(shift_left_logical_25_ll_shifted),
    .SUM(n32_bit_adder_23_sum));  // open: CarryOut
  _32_1_Bit_Multiplier u_32_1_bit_multiplier_27 (.A(A), .B(B[4]), .OM(n32_1_bit_multiplier_27_om));
  _32_1_Bit_Multiplier u_32_1_bit_multiplier_28 (.A(A), .B(B[5]), .OM(n32_1_bit_multiplier_28_om));
  Shift_Left_Logical shift_left_logical_28 (
    .A(n32_1_bit_multiplier_27_om), .S(5'b00100), .LL_SHIFTED(shift_left_logical_28_ll_shifted));
  _32_BIT_ADDER u_32_bit_adder_24 (
    .A(shift_left_logical_28_ll_shifted), .CarryIn0(1'b0), .B(shift_left_logical_26_ll_shifted),
    .SUM(n32_bit_adder_24_sum));  // open: CarryOut
  _32_BIT_ADDER u_32_bit_adder_25 (
    .A(n32_bit_adder_24_sum), .CarryIn0(1'b0), .B(n32_bit_adder_23_sum), .SUM(n32_bit_adder_25_sum));  // open: CarryOut
  _32_1_Bit_Multiplier u_32_1_bit_multiplier_29 (.A(A), .B(B[2]), .OM(n32_1_bit_multiplier_29_om));
  _32_1_Bit_Multiplier u_32_1_bit_multiplier_30 (.A(A), .B(B[3]), .OM(n32_1_bit_multiplier_30_om));
  Shift_Left_Logical shift_left_logical_29 (
    .A(n32_1_bit_multiplier_29_om), .S(5'b00010), .LL_SHIFTED(shift_left_logical_29_ll_shifted));
  Shift_Left_Logical shift_left_logical_30 (
    .A(n32_1_bit_multiplier_30_om), .S(5'b00011), .LL_SHIFTED(shift_left_logical_30_ll_shifted));
  _32_BIT_ADDER u_32_bit_adder_26 (
    .A(shift_left_logical_29_ll_shifted), .CarryIn0(1'b0), .B(shift_left_logical_30_ll_shifted),
    .SUM(n32_bit_adder_26_sum));  // open: CarryOut
  _32_1_Bit_Multiplier u_32_1_bit_multiplier_31 (.A(A), .B(B[1]), .OM(n32_1_bit_multiplier_31_om));
  Shift_Left_Logical shift_left_logical_31 (
    .A(n32_1_bit_multiplier_31_om), .S(5'b00001), .LL_SHIFTED(shift_left_logical_31_ll_shifted));
  _32_1_Bit_Multiplier u_32_1_bit_multiplier_32 (.A(A), .B(B[0]), .OM(n32_1_bit_multiplier_32_om));
  _32_BIT_ADDER u_32_bit_adder_27 (
    .A(n32_1_bit_multiplier_32_om), .CarryIn0(1'b0), .B(shift_left_logical_31_ll_shifted),
    .SUM(n32_bit_adder_27_sum));  // open: CarryOut
  _32_BIT_ADDER u_32_bit_adder_28 (
    .A(n32_bit_adder_27_sum), .CarryIn0(1'b0), .B(n32_bit_adder_26_sum), .SUM(n32_bit_adder_28_sum));  // open: CarryOut
  _32_BIT_ADDER u_32_bit_adder_29 (
    .A(n32_bit_adder_28_sum), .CarryIn0(1'b0), .B(n32_bit_adder_25_sum), .SUM(n32_bit_adder_29_sum));  // open: CarryOut
  _32_BIT_ADDER u_32_bit_adder_30 (
    .A(n32_bit_adder_29_sum), .CarryIn0(1'b0), .B(n32_bit_adder_22_sum), .SUM(n32_bit_adder_30_sum));  // open: CarryOut
  _32_BIT_ADDER u_32_bit_adder_31 (
    .A(n32_bit_adder_30_sum), .CarryIn0(1'b0), .B(n32_bit_adder_15_sum), .SUM(C));  // open: CarryOut

  // Other names for the same wires on the sheet: Print[31:0] = C
endmodule
