// Logisim project 32-Bit-EqualZero.circ as structural Verilog: 1 circuit, main circuit EqZero
module EqZero (
  input  [31:0] A,
  output out_2
);

  wire or_1_out;

  or or_1 (or_1_out, A[0], A[1], A[2], A[3], A[4], A[5], A[6], A[7], A[8], A[9], A[10], A[11], A[12], A[13], A[14], A[15], A[16], A[17], A[18], A[19], A[20], A[21], A[22], A[23], A[24], A[25], A[26], A[27], A[28], A[29], A[30], A[31]);
  not not_1 (out_2, or_1_out);
endmodule
