// Logisim project 32-Bit-MULT.circ as structural Verilog: 1 circuit, main circuit 32-Bit-MULT
module _32_Bit_MULT (
  input  [31:0] Multiplicand,
  input  [31:0] Multiplier,
  output [31:0] HIGH,
  output [31:0] LOW
);

  wire [31:0] _1_multiplicand_2, _1_new_sag, _1_new_shifted_sum, _2_multiplicand_2, _2_new_sag,
       _2_new_shifted_sum, _3_multiplicand_2, _3_new_sag, _3_new_shifted_sum, _4_multiplicand_2, _4_new_sag,
       _4_new_shifted_sum, _5_multiplicand_2, _5_new_sag, _5_new_shifted_sum, _6_multiplicand_2, _6_new_sag,
       _6_new_shifted_sum, _7_multiplicand_2, _7_new_sag, _7_new_shifted_sum, _8_multiplicand_2, _8_new_sag,
       _8_new_shifted_sum, _9_multiplicand_2, _9_new_sag, _9_new_shifted_sum, _10_multiplicand_2,
       _10_new_sag, _10_new_shifted_sum, _11_multiplicand_2, _11_new_sag, _11_new_shifted_sum,
       _12_multiplicand_2, _12_new_sag, _12_new_shifted_sum, _13_multiplicand_2, _13_new_sag,
       _13_new_shifted_sum, _14_multiplicand_2, _14_new_sag, _14_new_shifted_sum, _15_multiplicand_2,
       _15_new_sag, _15_new_shifted_sum, _16_multiplicand_2, _16_new_sag, _16_new_shifted_sum,
       _17_multiplicand_2, _17_new_sag, _17_new_shifted_sum, _18_multiplicand_2, _18_new_sag,
       _18_new_shifted_sum, _19_multiplicand_2, _19_new_sag, _19_new_shifted_sum, _20_multiplicand_2,
       _20_new_sag, _20_new_shifted_sum, _21_multiplicand_2, _21_new_sag, _21_new_shifted_sum,
       _22_multiplicand_2, _22_new_sag, _22_new_shifted_sum, _23_multiplicand_2, _23_new_sag,
       _23_new_shifted_sum, _24_multiplicand_2, _24_new_sag, _24_new_shifted_sum, _25_multiplicand_2,
       _25_new_sag, _25_new_shifted_sum, _26_multiplicand_2, _26_new_sag, _26_new_shifted_sum,
       _27_multiplicand_2, _27_new_sag, _27_new_shifted_sum, _28_multiplicand_2, _28_new_sag,
       _28_new_shifted_sum, _29_multiplicand_2, _29_new_sag, _29_new_shifted_sum, _30_multiplicand_2,
       _30_new_sag, _30_new_shifted_sum, _31_multiplicand_2, _31_new_sag, _31_new_shifted_sum;

  _32_Bit_Mult_Helper _1 (
    .PREV_SUM({32{1'b0}}), .MULTIPLICAND(Multiplicand), .SAG(Multiplier),
    .NEW_SHIFTED_SUM(_1_new_shifted_sum), .MULTIPLICAND_2(_1_multiplicand_2), .NEW_SAG(_1_new_sag));
  _32_Bit_Mult_Helper _2 (
    .PREV_SUM(_1_new_shifted_sum), .MULTIPLICAND(_1_multiplicand_2), .SAG(_1_new_sag),
    .NEW_SHIFTED_SUM(_2_new_shifted_sum), .MULTIPLICAND_2(_2_multiplicand_2), .NEW_SAG(_2_new_sag));
  _32_Bit_Mult_Helper _3 (
    .PREV_SUM(_2_new_shifted_sum), .MULTIPLICAND(_2_multiplicand_2), .SAG(_2_new_sag),
    .NEW_SHIFTED_SUM(_3_new_shifted_sum), .MULTIPLICAND_2(_3_multiplicand_2), .NEW_SAG(_3_new_sag));
  _32_Bit_Mult_Helper _18 (
    .PREV_SUM(_17_new_shifted_sum), .MULTIPLICAND(_17_multiplicand_2), .SAG(_17_new_sag),
    .NEW_SHIFTED_SUM(_18_new_shifted_sum), .MULTIPLICAND_2(_18_multiplicand_2), .NEW_SAG(_18_new_sag));
  _32_Bit_Mult_Helper _4 (
    .PREV_SUM(_3_new_shifted_sum), .MULTIPLICAND(_3_multiplicand_2), .SAG(_3_new_sag),
    .NEW_SHIFTED_SUM(_4_new_shifted_sum), .MULTIPLICAND_2(_4_multiplicand_2), .NEW_SAG(_4_new_sag));
  _32_Bit_Mult_Helper _19 (
    .PREV_SUM(_18_new_shifted_sum), .MULTIPLICAND(_18_multiplicand_2), .SAG(_18_new_sag),
    .NEW_SHIFTED_SUM(_19_new_shifted_sum), .MULTIPLICAND_2(_19_multiplicand_2), .NEW_SAG(_19_new_sag));
  _32_Bit_Mult_Helper _20 (
    .PREV_SUM(_19_new_shifted_sum), .MULTIPLICAND(_19_multiplicand_2), .SAG(_19_new_sag),
    .NEW_SHIFTED_SUM(_20_new_shifted_sum), .MULTIPLICAND_2(_20_multiplicand_2), .NEW_SAG(_20_new_sag));
  _32_Bit_Mult_Helper _5 (
    .PREV_SUM(_4_new_shifted_sum), .MULTIPLICAND(_4_multiplicand_2), .SAG(_4_new_sag),
    .NEW_SHIFTED_SUM(_5_new_shifted_sum), .MULTIPLICAND_2(_5_multiplicand_2), .NEW_SAG(_5_new_sag));
  _32_Bit_Mult_Helper _21 (
    .PREV_SUM(_20_new_shifted_sum), .MULTIPLICAND(_20_multiplicand_2), .SAG(_20_new_sag),
    .NEW_SHIFTED_SUM(_21_new_shifted_sum), .MULTIPLICAND_2(_21_multiplicand_2), .NEW_SAG(_21_new_sag));
  _32_Bit_Mult_Helper _6 (
    .PREV_SUM(_5_new_shifted_sum), .MULTIPLICAND(_5_multiplicand_2), .SAG(_5_new_sag),
    .NEW_SHIFTED_SUM(_6_new_shifted_sum), .MULTIPLICAND_2(_6_multiplicand_2), .NEW_SAG(_6_new_sag));
  _32_Bit_Mult_Helper _22 (
    .PREV_SUM(_21_new_shifted_sum), .MULTIPLICAND(_21_multiplicand_2), .SAG(_21_new_sag),
    .NEW_SHIFTED_SUM(_22_new_shifted_sum), .MULTIPLICAND_2(_22_multiplicand_2), .NEW_SAG(_22_new_sag));
  _32_Bit_Mult_Helper _7 (
    .PREV_SUM(_6_new_shifted_sum), .MULTIPLICAND(_6_multiplicand_2), .SAG(_6_new_sag),
    .NEW_SHIFTED_SUM(_7_new_shifted_sum), .MULTIPLICAND_2(_7_multiplicand_2), .NEW_SAG(_7_new_sag));
  _32_Bit_Mult_Helper _23 (
    .PREV_SUM(_22_new_shifted_sum), .MULTIPLICAND(_22_multiplicand_2), .SAG(_22_new_sag),
    .NEW_SHIFTED_SUM(_23_new_shifted_sum), .MULTIPLICAND_2(_23_multiplicand_2), .NEW_SAG(_23_new_sag));
  _32_Bit_Mult_Helper _8 (
    .PREV_SUM(_7_new_shifted_sum), .MULTIPLICAND(_7_multiplicand_2), .SAG(_7_new_sag),
    .NEW_SHIFTED_SUM(_8_new_shifted_sum), .MULTIPLICAND_2(_8_multiplicand_2), .NEW_SAG(_8_new_sag));
  _32_Bit_Mult_Helper _9 (
    .PREV_SUM(_8_new_shifted_sum), .MULTIPLICAND(_8_multiplicand_2), .SAG(_8_new_sag),
    .NEW_SHIFTED_SUM(_9_new_shifted_sum), .MULTIPLICAND_2(_9_multiplicand_2), .NEW_SAG(_9_new_sag));
  _32_Bit_Mult_Helper _24 (
    .PREV_SUM(_23_new_shifted_sum), .MULTIPLICAND(_23_multiplicand_2), .SAG(_23_new_sag),
    .NEW_SHIFTED_SUM(_24_new_shifted_sum), .MULTIPLICAND_2(_24_multiplicand_2), .NEW_SAG(_24_new_sag));
  _32_Bit_Mult_Helper _10 (
    .PREV_SUM(_9_new_shifted_sum), .MULTIPLICAND(_9_multiplicand_2), .SAG(_9_new_sag),
    .NEW_SHIFTED_SUM(_10_new_shifted_sum), .MULTIPLICAND_2(_10_multiplicand_2), .NEW_SAG(_10_new_sag));
  _32_Bit_Mult_Helper _25 (
    .PREV_SUM(_24_new_shifted_sum), .MULTIPLICAND(_24_multiplicand_2), .SAG(_24_new_sag),
    .NEW_SHIFTED_SUM(_25_new_shifted_sum), .MULTIPLICAND_2(_25_multiplicand_2), .NEW_SAG(_25_new_sag));
  _32_Bit_Mult_Helper _11 (
    .PREV_SUM(_10_new_shifted_sum), .MULTIPLICAND(_10_multiplicand_2), .SAG(_10_new_sag),
    .NEW_SHIFTED_SUM(_11_new_shifted_sum), .MULTIPLICAND_2(_11_multiplicand_2), .NEW_SAG(_11_new_sag));
  _32_Bit_Mult_Helper _26 (
    .PREV_SUM(_25_new_shifted_sum), .MULTIPLICAND(_25_multiplicand_2), .SAG(_25_new_sag),
    .NEW_SHIFTED_SUM(_26_new_shifted_sum), .MULTIPLICAND_2(_26_multiplicand_2), .NEW_SAG(_26_new_sag));
  _32_Bit_Mult_Helper _12 (
    .PREV_SUM(_11_new_shifted_sum), .MULTIPLICAND(_11_multiplicand_2), .SAG(_11_new_sag),
    .NEW_SHIFTED_SUM(_12_new_shifted_sum), .MULTIPLICAND_2(_12_multiplicand_2), .NEW_SAG(_12_new_sag));
  _32_Bit_Mult_Helper _28 (
    .PREV_SUM(_27_new_shifted_sum), .MULTIPLICAND(_27_multiplicand_2), .SAG(_27_new_sag),
    .NEW_SHIFTED_SUM(_28_new_shifted_sum), .MULTIPLICAND_2(_28_multiplicand_2), .NEW_SAG(_28_new_sag));
  _32_Bit_Mult_Helper _27 (
    .PREV_SUM(_26_new_shifted_sum), .MULTIPLICAND(_26_multiplicand_2), .SAG(_26_new_sag),
    .NEW_SHIFTED_SUM(_27_new_shifted_sum), .MULTIPLICAND_2(_27_multiplicand_2), .NEW_SAG(_27_new_sag));
  _32_Bit_Mult_Helper _13 (
    .PREV_SUM(_12_new_shifted_sum), .MULTIPLICAND(_12_multiplicand_2), .SAG(_12_new_sag),
    .NEW_SHIFTED_SUM(_13_new_shifted_sum), .MULTIPLICAND_2(_13_multiplicand_2), .NEW_SAG(_13_new_sag));
  _32_Bit_Mult_Helper _29 (
    .PREV_SUM(_28_new_shifted_sum), .MULTIPLICAND(_28_multiplicand_2), .SAG(_28_new_sag),
    .NEW_SHIFTED_SUM(_29_new_shifted_sum), .MULTIPLICAND_2(_29_multiplicand_2), .NEW_SAG(_29_new_sag));
  _32_Bit_Mult_Helper _14 (
    .PREV_SUM(_13_new_shifted_sum), .MULTIPLICAND(_13_multiplicand_2), .SAG(_13_new_sag),
    .NEW_SHIFTED_SUM(_14_new_shifted_sum), .MULTIPLICAND_2(_14_multiplicand_2), .NEW_SAG(_14_new_sag));
  _32_Bit_Mult_Helper _30 (
    .PREV_SUM(_29_new_shifted_sum), .MULTIPLICAND(_29_multiplicand_2), .SAG(_29_new_sag),
    .NEW_SHIFTED_SUM(_30_new_shifted_sum), .MULTIPLICAND_2(_30_multiplicand_2), .NEW_SAG(_30_new_sag));
  _32_Bit_Mult_Helper _15 (
    .PREV_SUM(_14_new_shifted_sum), .MULTIPLICAND(_14_multiplicand_2), .SAG(_14_new_sag),
    .NEW_SHIFTED_SUM(_15_new_shifted_sum), .MULTIPLICAND_2(_15_multiplicand_2), .NEW_SAG(_15_new_sag));
  _32_Bit_Mult_Helper _31 (
    .PREV_SUM(_30_new_shifted_sum), .MULTIPLICAND(_30_multiplicand_2), .SAG(_30_new_sag),
    .NEW_SHIFTED_SUM(_31_new_shifted_sum), .MULTIPLICAND_2(_31_multiplicand_2), .NEW_SAG(_31_new_sag));
  _32_Bit_Mult_Helper _17 (
    .PREV_SUM(_16_new_shifted_sum), .MULTIPLICAND(_16_multiplicand_2), .SAG(_16_new_sag),
    .NEW_SHIFTED_SUM(_17_new_shifted_sum), .MULTIPLICAND_2(_17_multiplicand_2), .NEW_SAG(_17_new_sag));
  _32_Bit_Mult_Helper _16 (
    .PREV_SUM(_15_new_shifted_sum), .MULTIPLICAND(_15_multiplicand_2), .SAG(_15_new_sag),
    .NEW_SHIFTED_SUM(_16_new_shifted_sum), .MULTIPLICAND_2(_16_multiplicand_2), .NEW_SAG(_16_new_sag));
  _32_Bit_Mult_Helper _32 (
    .PREV_SUM(_31_new_shifted_sum), .MULTIPLICAND(_31_multiplicand_2), .SAG(_31_new_sag),
    .NEW_SHIFTED_SUM(HIGH), .NEW_SAG(LOW));  // open: MULTIPLICAND_2
endmodule
