// Logisim project 32-Bit-Mult-Helper.circ as structural Verilog: 1 circuit, main circuit 32-Bit-Mult-Helper
module _32_Bit_Mult_Helper (
  input  [31:0] PREV_SUM,
  input  [31:0] MULTIPLICAND,
  input  [31:0] SAG,
  output [31:0] NEW_SHIFTED_SUM,
  output [31:0] MULTIPLICAND_2,
  output [31:0] NEW_SAG
);

  wire [31:0] multiplexer_1_out;
  wire [31:1] Adder_sum;
  wire [31:31] Shifter_ll_shifted;

  Multiplexer #(.width(32), .enable("false")) multiplexer_1 (
    .in0({32{1'b0}}), .in1(MULTIPLICAND), .out(multiplexer_1_out), .sel(SAG[0]));
  _32_BIT_ADDER Adder (
    .A(multiplexer_1_out), .CarryIn0(1'b0), .B(PREV_SUM), .SUM({Adder_sum, NEW_SAG[31]}));  // open: CarryOut
  Shift_Right_Local Shifter (.A(SAG), .S(5'b00001), .LL_SHIFTED({Shifter_ll_shifted[31], NEW_SAG[30:0]}));
  Shift_Right_Local Shifter_2 (.A({Adder_sum, NEW_SAG[31]}), .S(5'b00001), .LL_SHIFTED(NEW_SHIFTED_SUM));

  assign MULTIPLICAND_2 = MULTIPLICAND;

  // Other names for the same wires on the sheet: B[31:0] = SAG; M[31:0] = MULTIPLICAND; LSB = NEW_SAG[31]
endmodule
