// Logisim project 32-bit-adder-strange.circ as structural Verilog: 1 circuit, main circuit 32-BIT-ADDER
module _32_BIT_ADDER (
  input  [31:0] A,
  input  CarryIn0,
  input  [31:0] B,
  output CarryOut,
  output [31:0] SUM
);

  wire n1_bit_adder_1_carry_out, n1_bit_adder_2_carry_out, n1_bit_adder_3_carry_out,
       n1_bit_adder_4_carry_out, n1_bit_adder_5_carry_out, n1_bit_adder_6_carry_out,
       n1_bit_adder_7_carry_out, n1_bit_adder_8_carry_out, n1_bit_adder_9_carry_out,
       n1_bit_adder_10_carry_out, n1_bit_adder_11_carry_out, n1_bit_adder_12_carry_out,
       n1_bit_adder_13_carry_out, n1_bit_adder_14_carry_out, n1_bit_adder_15_carry_out,
       n1_bit_adder_16_carry_out, n1_bit_adder_17_carry_out, n1_bit_adder_18_carry_out,
       n1_bit_adder_19_carry_out, n1_bit_adder_20_carry_out, n1_bit_adder_21_carry_out,
       n1_bit_adder_22_carry_out, n1_bit_adder_23_carry_out, n1_bit_adder_24_carry_out,
       n1_bit_adder_25_carry_out, n1_bit_adder_26_carry_out, n1_bit_adder_27_carry_out,
       n1_bit_adder_28_carry_out, n1_bit_adder_29_carry_out, n1_bit_adder_30_carry_out,
       n1_bit_adder_31_carry_out;

  _1_BIT_ADDER u_1_bit_adder_1 (
    .A(B[0]), .B(A[0]), .Carry(CarryIn0), .Sum(SUM[0]), .Carry_Out(n1_bit_adder_1_carry_out));
  _1_BIT_ADDER u_1_bit_adder_2 (
    .A(B[1]), .B(A[1]), .Carry(n1_bit_adder_1_carry_out), .Sum(SUM[1]), .Carry_Out(n1_bit_adder_2_carry_out));
  _1_BIT_ADDER u_1_bit_adder_3 (
    .A(B[2]), .B(A[2]), .Carry(n1_bit_adder_2_carry_out), .Sum(SUM[2]), .Carry_Out(n1_bit_adder_3_carry_out));
  _1_BIT_ADDER u_1_bit_adder_4 (
    .A(B[3]), .B(A[3]), .Carry(n1_bit_adder_3_carry_out), .Sum(SUM[3]), .Carry_Out(n1_bit_adder_4_carry_out));
  _1_BIT_ADDER u_1_bit_adder_5 (
    .A(B[4]), .B(A[4]), .Carry(n1_bit_adder_4_carry_out), .Sum(SUM[4]), .Carry_Out(n1_bit_adder_5_carry_out));
  _1_BIT_ADDER u_1_bit_adder_6 (
    .A(B[5]), .B(A[5]), .Carry(n1_bit_adder_5_carry_out), .Sum(SUM[5]), .Carry_Out(n1_bit_adder_6_carry_out));
  _1_BIT_ADDER u_1_bit_adder_7 (
    .A(B[6]), .B(A[6]), .Carry(n1_bit_adder_6_carry_out), .Sum(SUM[6]), .Carry_Out(n1_bit_adder_7_carry_out));
  _1_BIT_ADDER u_1_bit_adder_8 (
    .A(B[8]), .B(A[8]), .Carry(n1_bit_adder_9_carry_out), .Sum(SUM[8]), .Carry_Out(n1_bit_adder_8_carry_out));
  _1_BIT_ADDER u_1_bit_adder_9 (
    .A(B[7]), .B(A[7]), .Carry(n1_bit_adder_7_carry_out), .Sum(SUM[7]), .Carry_Out(n1_bit_adder_9_carry_out));
  _1_BIT_ADDER u_1_bit_adder_10 (
    .A(B[9]), .B(A[9]), .Carry(n1_bit_adder_8_carry_out), .Sum(SUM[9]), .Carry_Out(n1_bit_adder_10_carry_out));
  _1_BIT_ADDER u_1_bit_adder_11 (
    .A(B[10]), .B(A[10]), .Carry(n1_bit_adder_10_carry_out), .Sum(SUM[10]),
    .Carry_Out(n1_bit_adder_11_carry_out));
  _1_BIT_ADDER u_1_bit_adder_12 (
    .A(B[11]), .B(A[11]), .Carry(n1_bit_adder_11_carry_out), .Sum(SUM[11]),
    .Carry_Out(n1_bit_adder_12_carry_out));
  _1_BIT_ADDER u_1_bit_adder_13 (
    .A(B[12]), .B(A[12]), .Carry(n1_bit_adder_12_carry_out), .Sum(SUM[12]),
    .Carry_Out(n1_bit_adder_13_carry_out));
  _1_BIT_ADDER u_1_bit_adder_14 (
    .A(B[13]), .B(A[13]), .Carry(n1_bit_adder_13_carry_out), .Sum(SUM[13]),
    .Carry_Out(n1_bit_adder_14_carry_out));
  _1_BIT_ADDER u_1_bit_adder_15 (
    .A(B[14]), .B(A[14]), .Carry(n1_bit_adder_14_carry_out), .Sum(SUM[14]),
    .Carry_Out(n1_bit_adder_15_carry_out));
  _1_BIT_ADDER u_1_bit_adder_16 (
    .A(B[15]), .B(A[15]), .Carry(n1_bit_adder_15_carry_out), .Sum(SUM[15]),
    .Carry_Out(n1_bit_adder_16_carry_out));
  _1_BIT_ADDER u_1_bit_adder_17 (
    .A(B[16]), .B(A[16]), .Carry(n1_bit_adder_16_carry_out), .Sum(SUM[16]),
    .Carry_Out(n1_bit_adder_17_carry_out));
  _1_BIT_ADDER u_1_bit_adder_18 (
    .A(B[17]), .B(A[17]), .Carry(n1_bit_adder_17_carry_out), .Sum(SUM[17]),
    .Carry_Out(n1_bit_adder_18_carry_out));
  _1_BIT_ADDER u_1_bit_adder_19 (
    .A(B[18]), .B(A[18]), .Carry(n1_bit_adder_18_carry_out), .Sum(SUM[18]),
    .Carry_Out(n1_bit_adder_19_carry_out));
  _1_BIT_ADDER u_1_bit_adder_20 (
    .A(B[19]), .B(A[19]), .Carry(n1_bit_adder_19_carry_out), .Sum(SUM[19]),
    .Carry_Out(n1_bit_adder_20_carry_out));
  _1_BIT_ADDER u_1_bit_adder_21 (
    .A(B[20]), .B(A[20]), .Carry(n1_bit_adder_20_carry_out), .Sum(SUM[20]),
    .Carry_Out(n1_bit_adder_21_carry_out));
  _1_BIT_ADDER u_1_bit_adder_22 (
    .A(B[21]), .B(A[21]), .Carry(n1_bit_adder_21_carry_out), .Sum(SUM[21]),
    .Carry_Out(n1_bit_adder_22_carry_out));
  _1_BIT_ADDER u_1_bit_adder_23 (
    .A(B[22]), .B(A[22]), .Carry(n1_bit_adder_22_carry_out), .Sum(SUM[22]),
    .Carry_Out(n1_bit_adder_23_carry_out));
  _1_BIT_ADDER u_1_bit_adder_24 (
    .A(B[23]), .B(A[23]), .Carry(n1_bit_adder_23_carry_out), .Sum(SUM[23]),
    .Carry_Out(n1_bit_adder_24_carry_out));
  _1_BIT_ADDER u_1_bit_adder_25 (
    .A(B[24]), .B(A[24]), .Carry(n1_bit_adder_24_carry_out), .Sum(SUM[24]),
    .Carry_Out(n1_bit_adder_25_carry_out));
  _1_BIT_ADDER u_1_bit_adder_26 (
    .A(B[25]), .B(A[25]), .Carry(n1_bit_adder_25_carry_out), .Sum(SUM[25]),
    .Carry_Out(n1_bit_adder_26_carry_out));
  _1_BIT_ADDER u_1_bit_adder_27 (
    .A(B[27]), .B(A[27]), .Carry(n1_bit_adder_28_carry_out), .Sum(SUM[27]),
    .Carry_Out(n1_bit_adder_27_carry_out));
  _1_BIT_ADDER u_1_bit_adder_28 (
    .A(B[26]), .B(A[26]), .Carry(n1_bit_adder_26_carry_out), .Sum(SUM[26]),
    .Carry_Out(n1_bit_adder_28_carry_out));
  _1_BIT_ADDER u_1_bit_adder_29 (
    .A(B[28]), .B(A[28]), .Carry(n1_bit_adder_27_carry_out), .Sum(SUM[28]),
    .Carry_Out(n1_bit_adder_29_carry_out));
  _1_BIT_ADDER u_1_bit_adder_30 (
    .A(B[30]), .B(A[30]), .Carry(n1_bit_adder_31_carry_out), .Sum(SUM[30]),
    .Carry_Out(n1_bit_adder_30_carry_out));
  _1_BIT_ADDER u_1_bit_adder_31 (
    .A(B[29]), .B(A[29]), .Carry(n1_bit_adder_29_carry_out), .Sum(SUM[29]),
    .Carry_Out(n1_bit_adder_31_carry_out));
  _1_BIT_ADDER u_1_bit_adder_32 (
    .A(B[31]), .B(A[31]), .Carry(n1_bit_adder_30_carry_out), .Sum(SUM[31]), .Carry_Out(CarryOut));
endmodule
