// Logisim project Shift-Left-Logical.circ as structural Verilog: 1 circuit, main circuit Shift-Left-Logical
module Shift_Left_Logical (
  input  [31:0] A,
  input  [4:0] S,
  output [31:0] LL_SHIFTED
);

  wire B0, B1, B2, B3, B4, B5, B6, B7, B8, B9, B10, B11, B12, B13, B14, B15, B16, B17, B18, B19, B20, B21,
       B22, B23, B24, B25, B26, B27, B28, B29, B30, B31, C0, C1, C2, C3, C4, C5, C6, C7, C8, C9, C10, C11,
       C12, C13, C14, C15, C16, C17, C18, C19, C20, C21, C22, C23, C24, C25, C26, C27, C28, C29, C30, C31,
       E0, E1, E2, E3, E4, E5, E6, E7, E8, E9, E10, E11, E12, E13, E14, E15, E16, E17, E18, E19, E20, E21,
       E22, E23, E24, E25, E26, E27, E28, E29, E30, E31, F0, F1, F2, F3, F4, F5, F6, F7, F8, F9, F10, F11,
       F12, F13, F14, F15, F16, F17, F18, F19, F20, F21, F22, F23, F24, F25, F26, F27, F28, F29, F30, F31;

  Multiplexer multiplexer_1 (.in0(A[31]), .in1(A[30]), .out(B0), .sel(S[0]), .en(1'b1));
  Multiplexer multiplexer_2 (.in0(A[30]), .in1(A[29]), .out(B1), .sel(S[0]), .en(1'b1));
  Multiplexer multiplexer_3 (.in0(A[29]), .in1(A[28]), .out(B2), .sel(S[0]), .en(1'b1));
  Multiplexer multiplexer_4 (.in0(A[28]), .in1(A[27]), .out(B3), .sel(S[0]), .en(1'b1));
  Multiplexer multiplexer_5 (.in0(A[27]), .in1(A[26]), .out(B4), .sel(S[0]), .en(1'b1));
  Multiplexer multiplexer_6 (.in0(A[26]), .in1(A[25]), .out(B5), .sel(S[0]), .en(1'b1));
  Multiplexer multiplexer_7 (.in0(A[25]), .in1(A[24]), .out(B6), .sel(S[0]), .en(1'b1));
  Multiplexer multiplexer_8 (.in0(A[24]), .in1(A[23]), .out(B7), .sel(S[0]), .en(1'b1));
  Multiplexer multiplexer_9 (.in0(A[23]), .in1(A[22]), .out(B8), .sel(S[0]), .en(1'b1));
  Multiplexer multiplexer_10 (.in0(A[22]), .in1(A[21]), .out(B9), .sel(S[0]), .en(1'b1));
  Multiplexer multiplexer_11 (.in0(A[21]), .in1(A[20]), .out(B10), .sel(S[0]), .en(1'b1));
  Multiplexer multiplexer_12 (.in0(A[20]), .in1(A[19]), .out(B11), .sel(S[0]), .en(1'b1));
  Multiplexer multiplexer_13 (.in0(A[19]), .in1(A[18]), .out(B12), .sel(S[0]), .en(1'b1));
  Multiplexer multiplexer_14 (.in0(A[18]), .in1(A[17]), .out(B13), .sel(S[0]), .en(1'b1));
  Multiplexer multiplexer_15 (.in0(A[17]), .in1(A[16]), .out(B14), .sel(S[0]), .en(1'b1));
  Multiplexer multiplexer_16 (.in0(A[16]), .in1(A[15]), .out(B15), .sel(S[0]), .en(1'b1));
  Multiplexer multiplexer_17 (.in0(A[15]), .in1(A[14]), .out(B16), .sel(S[0]), .en(1'b1));
  Multiplexer multiplexer_18 (.in0(A[14]), .in1(A[13]), .out(B17), .sel(S[0]), .en(1'b1));
  Multiplexer multiplexer_19 (.in0(A[13]), .in1(A[12]), .out(B18), .sel(S[0]), .en(1'b1));
  Multiplexer multiplexer_20 (.in0(A[12]), .in1(A[11]), .out(B19), .sel(S[0]), .en(1'b1));
  Multiplexer multiplexer_21 (.in0(A[11]), .in1(A[10]), .out(B20), .sel(S[0]), .en(1'b1));
  Multiplexer multiplexer_22 (.in0(A[10]), .in1(A[9]), .out(B21), .sel(S[0]), .en(1'b1));
  Multiplexer multiplexer_23 (.in0(A[9]), .in1(A[8]), .out(B22), .sel(S[0]), .en(1'b1));
  Multiplexer multiplexer_24 (.in0(A[8]), .in1(A[7]), .out(B23), .sel(S[0]), .en(1'b1));
  Multiplexer multiplexer_25 (.in0(A[7]), .in1(A[6]), .out(B24), .sel(S[0]), .en(1'b1));
  Multiplexer multiplexer_26 (.in0(A[6]), .in1(A[5]), .out(B25), .sel(S[0]), .en(1'b1));
  Multiplexer multiplexer_27 (.in0(A[5]), .in1(A[4]), .out(B26), .sel(S[0]), .en(1'b1));
  Multiplexer multiplexer_28 (.in0(A[4]), .in1(A[3]), .out(B27), .sel(S[0]), .en(1'b1));
  Multiplexer multiplexer_29 (.in0(A[3]), .in1(A[2]), .out(B28), .sel(S[0]), .en(1'b1));
  Multiplexer multiplexer_30 (.in0(A[2]), .in1(A[1]), .out(B29), .sel(S[0]), .en(1'b1));
  Multiplexer multiplexer_31 (.in0(A[1]), .in1(A[0]), .out(B30), .sel(S[0]), .en(1'b1));
  Multiplexer multiplexer_32 (.in0(A[0]), .in1(1'b0), .out(B31), .sel(S[0]), .en(1'b1));
  Multiplexer multiplexer_33 (.in0(B0), .in1(B2), .out(C0), .sel(S[1]), .en(1'b1));
  Multiplexer multiplexer_34 (.in0(B1), .in1(B3), .out(C1), .sel(S[1]), .en(1'b1));
  Multiplexer multiplexer_35 (.in0(B2), .in1(B4), .out(C2), .sel(S[1]), .en(1'b1));
  Multiplexer multiplexer_36 (.in0(B3), .in1(B5), .out(C3), .sel(S[1]), .en(1'b1));
  Multiplexer multiplexer_37 (.in0(B4), .in1(B6), .out(C4), .sel(S[1]), .en(1'b1));
  Multiplexer multiplexer_38 (.in0(B5), .in1(B7), .out(C5), .sel(S[1]), .en(1'b1));
  Multiplexer multiplexer_39 (.in0(B6), .in1(B8), .out(C6), .sel(S[1]), .en(1'b1));
  Multiplexer multiplexer_40 (.in0(B7), .in1(B9), .out(C7), .sel(S[1]), .en(1'b1));
  Multiplexer multiplexer_41 (.in0(B8), .in1(B10), .out(C8), .sel(S[1]), .en(1'b1));
  Multiplexer multiplexer_42 (.in0(B9), .in1(B11), .out(C9), .sel(S[1]), .en(1'b1));
  Multiplexer multiplexer_43 (.in0(B10), .in1(B12), .out(C10), .sel(S[1]), .en(1'b1));
  Multiplexer multiplexer_44 (.in0(B11), .in1(B13), .out(C11), .sel(S[1]), .en(1'b1));
  Multiplexer multiplexer_45 (.in0(B12), .in1(B14), .out(C12), .sel(S[1]), .en(1'b1));
  Multiplexer multiplexer_46 (.in0(B13), .in1(B15), .out(C13), .sel(S[1]), .en(1'b1));
  Multiplexer multiplexer_47 (.in0(B14), .in1(B16), .out(C14), .sel(S[1]), .en(1'b1));
  Multiplexer multiplexer_48 (.in0(B15), .in1(B17), .out(C15), .sel(S[1]), .en(1'b1));
  Multiplexer multiplexer_49 (.in0(B16), .in1(B18), .out(C16), .sel(S[1]), .en(1'b1));
  Multiplexer multiplexer_50 (.in0(B17), .in1(B19), .out(C17), .sel(S[1]), .en(1'b1));
  Multiplexer multiplexer_51 (.in0(B18), .in1(B20), .out(C18), .sel(S[1]), .en(1'b1));
  Multiplexer multiplexer_52 (.in0(B19), .in1(B21), .out(C19), .sel(S[1]), .en(1'b1));
  Multiplexer multiplexer_53 (.in0(B20), .in1(B22), .out(C20), .sel(S[1]), .en(1'b1));
  Multiplexer multiplexer_54 (.in0(B21), .in1(B23), .out(C21), .sel(S[1]), .en(1'b1));
  Multiplexer multiplexer_55 (.in0(B22), .in1(B24), .out(C22), .sel(S[1]), .en(1'b1));
  Multiplexer multiplexer_56 (.in0(B23), .in1(B25), .out(C23), .sel(S[1]), .en(1'b1));
  Multiplexer multiplexer_57 (.in0(B24), .in1(B26), .out(C24), .sel(S[1]), .en(1'b1));
  Multiplexer multiplexer_58 (.in0(B25), .in1(B27), .out(C25), .sel(S[1]), .en(1'b1));
  Multiplexer multiplexer_59 (.in0(B26), .in1(B28), .out(C26), .sel(S[1]), .en(1'b1));
  Multiplexer multiplexer_60 (.in0(B27), .in1(B29), .out(C27), .sel(S[1]), .en(1'b1));
  Multiplexer multiplexer_61 (.in0(B28), .in1(B30), .out(C28), .sel(S[1]), .en(1'b1));
  Multiplexer multiplexer_62 (.in0(B29), .in1(B31), .out(C29), .sel(S[1]), .en(1'b1));
  Multiplexer multiplexer_63 (.in0(B30), .in1(1'b0), .out(C30), .sel(S[1]), .en(1'b1));
  Multiplexer multiplexer_64 (.in0(B31), .in1(1'b0), .out(C31), .sel(S[1]), .en(1'b1));
  Multiplexer multiplexer_65 (.in0(C0), .in1(C4), .out(E0), .sel(S[2]), .en(1'b1));
  Multiplexer multiplexer_66 (.in0(C1), .in1(C5), .out(E1), .sel(S[2]), .en(1'b1));
  Multiplexer multiplexer_67 (.in0(C2), .in1(C6), .out(E2), .sel(S[2]), .en(1'b1));
  Multiplexer multiplexer_68 (.in0(C3), .in1(C7), .out(E3), .sel(S[2]), .en(1'b1));
  Multiplexer multiplexer_69 (.in0(C4), .in1(C8), .out(E4), .sel(S[2]), .en(1'b1));
  Multiplexer multiplexer_70 (.in0(C5), .in1(C9), .out(E5), .sel(S[2]), .en(1'b1));
  Multiplexer multiplexer_71 (.in0(C6), .in1(C10), .out(E6), .sel(S[2]), .en(1'b1));
  Multiplexer multiplexer_72 (.in0(C7), .in1(C11), .out(E7), .sel(S[2]), .en(1'b1));
  Multiplexer multiplexer_73 (.in0(C8), .in1(C12), .out(E8), .sel(S[2]), .en(1'b1));
  Multiplexer multiplexer_74 (.in0(C9), .in1(C13), .out(E9), .sel(S[2]), .en(1'b1));
  Multiplexer multiplexer_75 (.in0(C10), .in1(C14), .out(E10), .sel(S[2]), .en(1'b1));
  Multiplexer multiplexer_76 (.in0(C11), .in1(C15), .out(E11), .sel(S[2]), .en(1'b1));
  Multiplexer multiplexer_77 (.in0(C12), .in1(C16), .out(E12), .sel(S[2]), .en(1'b1));
  Multiplexer multiplexer_78 (.in0(C13), .in1(C17), .out(E13), .sel(S[2]), .en(1'b1));
  Multiplexer multiplexer_79 (.in0(C14), .in1(C18), .out(E14), .sel(S[2]), .en(1'b1));
  Multiplexer multiplexer_80 (.in0(C15), .in1(C19), .out(E15), .sel(S[2]), .en(1'b1));
  Multiplexer multiplexer_81 (.in0(C16), .in1(C20), .out(E16), .sel(S[2]), .en(1'b1));
  Multiplexer multiplexer_82 (.in0(C17), .in1(C21), .out(E17), .sel(S[2]), .en(1'b1));
  Multiplexer multiplexer_83 (.in0(C18), .in1(C22), .out(E18), .sel(S[2]), .en(1'b1));
  Multiplexer multiplexer_84 (.in0(C19), .in1(C23), .out(E19), .sel(S[2]), .en(1'b1));
  Multiplexer multiplexer_85 (.in0(C20), .in1(C24), .out(E20), .sel(S[2]), .en(1'b1));
  Multiplexer multiplexer_86 (.in0(C21), .in1(C25), .out(E21), .sel(S[2]), .en(1'b1));
  Multiplexer multiplexer_87 (.in0(C22), .in1(C26), .out(E22), .sel(S[2]), .en(1'b1));
  Multiplexer multiplexer_88 (.in0(C23), .in1(C27), .out(E23), .sel(S[2]), .en(1'b1));
  Multiplexer multiplexer_89 (.in0(C24), .in1(C28), .out(E24), .sel(S[2]), .en(1'b1));
  Multiplexer multiplexer_90 (.in0(C25), .in1(C29), .out(E25), .sel(S[2]), .en(1'b1));
  Multiplexer multiplexer_91 (.in0(C26), .in1(C30), .out(E26), .sel(S[2]), .en(1'b1));
  Multiplexer multiplexer_92 (.in0(C27), .in1(C31), .out(E27), .sel(S[2]), .en(1'b1));
  Multiplexer multiplexer_93 (.in0(C28), .in1(1'b0), .out(E28), .sel(S[2]), .en(1'b1));
  Multiplexer multiplexer_94 (.in0(C29), .in1(1'b0), .out(E29), .sel(S[2]), .en(1'b1));
  Multiplexer multiplexer_95 (.in0(C30), .in1(1'b0), .out(E30), .sel(S[2]), .en(1'b1));
  Multiplexer multiplexer_96 (.in0(C31), .in1(1'b0), .out(E31), .sel(S[2]), .en(1'b1));
  Multiplexer multiplexer_97 (.in0(E0), .in1(E8), .out(F0), .sel(S[3]), .en(1'b1));
  Multiplexer multiplexer_98 (.in0(E1), .in1(E9), .out(F1), .sel(S[3]), .en(1'b1));
  Multiplexer multiplexer_99 (.in0(E2), .in1(E10), .out(F2), .sel(S[3]), .en(1'b1));
  Multiplexer multiplexer_100 (.in0(E3), .in1(E11), .out(F3), .sel(S[3]), .en(1'b1));
  Multiplexer multiplexer_101 (.in0(E4), .in1(E12), .out(F4), .sel(S[3]), .en(1'b1));
  Multiplexer multiplexer_102 (.in0(E5), .in1(E13), .out(F5), .sel(S[3]), .en(1'b1));
  Multiplexer multiplexer_103 (.in0(E6), .in1(E14), .out(F6), .sel(S[3]), .en(1'b1));
  Multiplexer multiplexer_104 (.in0(E7), .in1(E15), .out(F7), .sel(S[3]), .en(1'b1));
  Multiplexer multiplexer_105 (.in0(E8), .in1(E16), .out(F8), .sel(S[3]), .en(1'b1));
  Multiplexer multiplexer_106 (.in0(E9), .in1(E17), .out(F9), .sel(S[3]), .en(1'b1));
  Multiplexer multiplexer_107 (.in0(E10), .in1(E18), .out(F10), .sel(S[3]), .en(1'b1));
  Multiplexer multiplexer_108 (.in0(E11), .in1(E19), .out(F11), .sel(S[3]), .en(1'b1));
  Multiplexer multiplexer_109 (.in0(E12), .in1(E20), .out(F12), .sel(S[3]), .en(1'b1));
  Multiplexer multiplexer_110 (.in0(E13), .in1(E21), .out(F13), .sel(S[3]), .en(1'b1));
  Multiplexer multiplexer_111 (.in0(E14), .in1(E22), .out(F14), .sel(S[3]), .en(1'b1));
  Multiplexer multiplexer_112 (.in0(E15), .in1(E23), .out(F15), .sel(S[3]), .en(1'b1));
  Multiplexer multiplexer_113 (.in0(E16), .in1(E24), .out(F16), .sel(S[3]), .en(1'b1));
  Multiplexer multiplexer_114 (.in0(E17), .in1(E25), .out(F17), .sel(S[3]), .en(1'b1));
  Multiplexer multiplexer_115 (.in0(E18), .in1(E26), .out(F18), .sel(S[3]), .en(1'b1));
  Multiplexer multiplexer_116 (.in0(E19), .in1(E27), .out(F19), .sel(S[3]), .en(1'b1));
  Multiplexer multiplexer_117 (.in0(E20), .in1(E28), .out(F20), .sel(S[3]), .en(1'b1));
  Multiplexer multiplexer_118 (.in0(E21), .in1(E29), .out(F21), .sel(S[3]), .en(1'b1));
  Multiplexer multiplexer_119 (.in0(E22), .in1(E30), .out(F22), .sel(S[3]), .en(1'b1));
  Multiplexer multiplexer_120 (.in0(E23), .in1(E31), .out(F23), .sel(S[3]), .en(1'b1));
  Multiplexer multiplexer_121 (.in0(E24), .in1(1'b0), .out(F24), .sel(S[3]), .en(1'b1));
  Multiplexer multiplexer_122 (.in0(E25), .in1(1'b0), .out(F25), .sel(S[3]), .en(1'b1));
  Multiplexer multiplexer_123 (.in0(E26), .in1(1'b0), .out(F26), .sel(S[3]), .en(1'b1));
  Multiplexer multiplexer_124 (.in0(E27), .in1(1'b0), .out(F27), .sel(S[3]), .en(1'b1));
  Multiplexer multiplexer_125 (.in0(E28), .in1(1'b0), .out(F28), .sel(S[3]), .en(1'b1));
  Multiplexer multiplexer_126 (.in0(E29), .in1(1'b0), .out(F29), .sel(S[3]), .en(1'b1));
  Multiplexer multiplexer_127 (.in0(E30), .in1(1'b0), .out(F30), .sel(S[3]), .en(1'b1));
  Multiplexer multiplexer_128 (.in0(E31), .in1(1'b0), .out(F31), .sel(S[3]), .en(1'b1));
  Multiplexer multiplexer_129 (.in0(F0), .in1(F16), .out(LL_SHIFTED[31]), .sel(S[4]), .en(1'b1));
  Multiplexer multiplexer_130 (.in0(F1), .in1(F17), .out(LL_SHIFTED[30]), .sel(S[4]), .en(1'b1));
  Multiplexer multiplexer_131 (.in0(F2), .in1(F18), .out(LL_SHIFTED[29]), .sel(S[4]), .en(1'b1));
  Multiplexer multiplexer_132 (.in0(F3), .in1(F19), .out(LL_SHIFTED[28]), .sel(S[4]), .en(1'b1));
  Multiplexer multiplexer_133 (.in0(F4), .in1(F20), .out(LL_SHIFTED[27]), .sel(S[4]), .en(1'b1));
  Multiplexer multiplexer_134 (.in0(F5), .in1(F21), .out(LL_SHIFTED[26]), .sel(S[4]), .en(1'b1));
  Multiplexer multiplexer_135 (.in0(F6), .in1(F22), .out(LL_SHIFTED[25]), .sel(S[4]), .en(1'b1));
  Multiplexer multiplexer_136 (.in0(F7), .in1(F23), .out(LL_SHIFTED[24]), .sel(S[4]), .en(1'b1));
  Multiplexer multiplexer_137 (.in0(F8), .in1(F24), .out(LL_SHIFTED[23]), .sel(S[4]), .en(1'b1));
  Multiplexer multiplexer_138 (.in0(F9), .in1(F25), .out(LL_SHIFTED[22]), .sel(S[4]), .en(1'b1));
  Multiplexer multiplexer_139 (.in0(F10), .in1(F26), .out(LL_SHIFTED[21]), .sel(S[4]), .en(1'b1));
  Multiplexer multiplexer_140 (.in0(F11), .in1(F27), .out(LL_SHIFTED[20]), .sel(S[4]), .en(1'b1));
  Multiplexer multiplexer_141 (.in0(F12), .in1(F28), .out(LL_SHIFTED[19]), .sel(S[4]), .en(1'b1));
  Multiplexer multiplexer_142 (.in0(F13), .in1(F29), .out(LL_SHIFTED[18]), .sel(S[4]), .en(1'b1));
  Multiplexer multiplexer_143 (.in0(F14), .in1(F30), .out(LL_SHIFTED[17]), .sel(S[4]), .en(1'b1));
  Multiplexer multiplexer_144 (.in0(F15), .in1(F31), .out(LL_SHIFTED[16]), .sel(S[4]), .en(1'b1));
  Multiplexer multiplexer_145 (.in0(F16), .in1(1'b0), .out(LL_SHIFTED[15]), .sel(S[4]), .en(1'b1));
  Multiplexer multiplexer_146 (.in0(F17), .in1(1'b0), .out(LL_SHIFTED[14]), .sel(S[4]), .en(1'b1));
  Multiplexer multiplexer_147 (.in0(F18), .in1(1'b0), .out(LL_SHIFTED[13]), .sel(S[4]), .en(1'b1));
  Multiplexer multiplexer_148 (.in0(F19), .in1(1'b0), .out(LL_SHIFTED[12]), .sel(S[4]), .en(1'b1));
  Multiplexer multiplexer_149 (.in0(F20), .in1(1'b0), .out(LL_SHIFTED[11]), .sel(S[4]), .en(1'b1));
  Multiplexer multiplexer_150 (.in0(F21), .in1(1'b0), .out(LL_SHIFTED[10]), .sel(S[4]), .en(1'b1));
  Multiplexer multiplexer_151 (.in0(F22), .in1(1'b0), .out(LL_SHIFTED[9]), .sel(S[4]), .en(1'b1));
  Multiplexer multiplexer_152 (.in0(F23), .in1(1'b0), .out(LL_SHIFTED[8]), .sel(S[4]), .en(1'b1));
  Multiplexer multiplexer_153 (.in0(F24), .in1(1'b0), .out(LL_SHIFTED[7]), .sel(S[4]), .en(1'b1));
  Multiplexer multiplexer_154 (.in0(F25), .in1(1'b0), .out(LL_SHIFTED[6]), .sel(S[4]), .en(1'b1));
  Multiplexer multiplexer_155 (.in0(F26), .in1(1'b0), .out(LL_SHIFTED[5]), .sel(S[4]), .en(1'b1));
  Multiplexer multiplexer_156 (.in0(F27), .in1(1'b0), .out(LL_SHIFTED[4]), .sel(S[4]), .en(1'b1));
  Multiplexer multiplexer_157 (.in0(F28), .in1(1'b0), .out(LL_SHIFTED[3]), .sel(S[4]), .en(1'b1));
  Multiplexer multiplexer_158 (.in0(F29), .in1(1'b0), .out(LL_SHIFTED[2]), .sel(S[4]), .en(1'b1));
  Multiplexer multiplexer_159 (.in0(F30), .in1(1'b0), .out(LL_SHIFTED[1]), .sel(S[4]), .en(1'b1));
  Multiplexer multiplexer_160 (.in0(F31), .in1(1'b0), .out(LL_SHIFTED[0]), .sel(S[4]), .en(1'b1));

  // Other names for the same wires on the sheet: A31 = A[0]; A30 = A[1]; A29 = A[2]; A28 = A[3]; A27 = A[4];
  //   A26 = A[5]; A25 = A[6]; A24 = A[7]; A23 = A[8]; A22 = A[9]; A21 = A[10]; A20 = A[11]; A19 = A[12]; A18 = A[13];
  //   A17 = A[14]; A16 = A[15]; A15 = A[16]; A14 = A[17]; A13 = A[18]; A12 = A[19]; A11 = A[20]; A10 = A[21];
  //   A9 = A[22]; A8 = A[23]; A7 = A[24]; A6 = A[25]; A5 = A[26]; A4 = A[27]; A3 = A[28]; A2 = A[29]; A1 = A[30];
  //   A0 = A[31]; D31 = LL_SHIFTED[0]; D30 = LL_SHIFTED[1]; D29 = LL_SHIFTED[2]; D28 = LL_SHIFTED[3];
  //   D27 = LL_SHIFTED[4]; D26 = LL_SHIFTED[5]; D25 = LL_SHIFTED[6]; D24 = LL_SHIFTED[7]; D23 = LL_SHIFTED[8];
  //   D22 = LL_SHIFTED[9]; D21 = LL_SHIFTED[10]; D20 = LL_SHIFTED[11]; D19 = LL_SHIFTED[12]; D18 = LL_SHIFTED[13];
  //   D17 = LL_SHIFTED[14]; D16 = LL_SHIFTED[15]; D15 = LL_SHIFTED[16]; D14 = LL_SHIFTED[17]; D13 = LL_SHIFTED[18];
  //   D12 = LL_SHIFTED[19]; D11 = LL_SHIFTED[20]; D10 = LL_SHIFTED[21]; D9 = LL_SHIFTED[22]; D8 = LL_SHIFTED[23];
  //   D7 = LL_SHIFTED[24]; D6 = LL_SHIFTED[25]; D5 = LL_SHIFTED[26]; D4 = LL_SHIFTED[27]; D3 = LL_SHIFTED[28];
  //   D2 = LL_SHIFTED[29]; D1 = LL_SHIFTED[30]; D0 = LL_SHIFTED[31]
endmodule
