// Logisim project SingcleCycleProcessorPC+1.circ as structural Verilog: 1 circuit, main circuit main
module main (
);

  wire and_1_out, and_2_out, CLK, decoder_1_out0, decoder_1_out1, decoder_1_out2, decoder_1_out3,
       decoder_1_out4, decoder_1_out5, decoder_1_out6, decoder_1_out7, decoder_1_out8, decoder_1_out9,
       main_1_zero, not_1_out, or_2_out, SIG_ADDI, SIG_ALU_OP, SIG_ALUSrc, SIG_BEQ, SIG_BNE, SIG_JUMP,
       SIG_MEM_READ, SIG_MemWrite, SIG_RegWrite;
  wire [3:0] bitselector_2_out, bitselector_4_out, multiplexer_1_out;
  wire [4:0] multiplexer_2_out, RD, RS, RT, SHAMT;
  wire [5:0] ALU_CONTROL_MUX_INPUT, FUNCT, OPCODE;
  wire [23:0] bitselector_1_out, bitselector_5_out, PC_q;
  wire [25:0] bitselector_3_out;
  wire [31:0] ALU_RESULT, B, bit_extender_1_out, JUMP_ADDRESS, multiplexer_3_out, multiplexer_4_out,
       n32_bit_adder_1_sum, NEW_PC, PC_1, ram_1_data, registerfile_1_p7, SIGN_EXTENDED, WRITEBACK;

  BitSelector #(.width(32), .group(24)) bitselector_1 (.in(NEW_PC), .out(bitselector_1_out), .sel(1'b0));
  // Probe on NEW_PC
  assign bit_extender_1_out = {{8{1'b0}}, PC_q};  // Bit_Extender bit_extender_1
  Counter #(.width(24), .max('hffffff)) PC (
    .load(1'b1), .D(bitselector_1_out), .count(1'b0), .Q(PC_q), .clk(CLK));  // open: carry, clr
  assign SIGN_EXTENDED = {{16{1'b0}}, {RD, SHAMT, FUNCT}};  // Bit_Extender bit_extender_2
  Clock SPIRIT_OF_LIFE (.out(CLK));
  // Probe on bit_extender_1_out
  _32_BIT_ADDER u_32_bit_adder_1 (
    .A(bit_extender_1_out), .CarryIn0(1'b0), .B(32'h1), .SUM(n32_bit_adder_1_sum));  // open: CarryOut
  // Probe on 32'h1
  // Probe on n32_bit_adder_1_sum
  Adder #(.width(32)) adder_1 (.a(bit_extender_1_out), .b(32'h1), .out(PC_1), .cin(1'b0));  // open: cout
  ROM #(.addrWidth(24), .dataWidth(32)) rom_1 (.addr(PC_q), .data({OPCODE, RS, RT, RD, SHAMT, FUNCT}), .sel(1'b1));
  BitSelector #(.width(6), .group(4)) bitselector_2 (.in(OPCODE), .out(bitselector_2_out), .sel(1'b0));
  BitSelector #(.width(32), .group(26)) bitselector_3 (
    .in({OPCODE, RS, RT, RD, SHAMT, FUNCT}), .out(bitselector_3_out), .sel(1'b0));
  // Probe on PC_1
  assign JUMP_ADDRESS = {{6{1'b0}}, bitselector_3_out};  // Bit_Extender bit_extender_3
  BitSelector #(.width(6), .group(4)) bitselector_4 (.in(OPCODE), .out(bitselector_4_out), .sel(1'b0));
  Multiplexer #(.select(4), .width(4), .enable("false")) multiplexer_1 (
    .in0(bitselector_2_out), .in1(bitselector_2_out), .in2(bitselector_2_out), .in3(bitselector_2_out),
    .in4(bitselector_2_out), .in5(bitselector_2_out), .in6(bitselector_2_out), .in7(bitselector_2_out),
    .in8(bitselector_2_out), .in9(bitselector_2_out), .in10(4'b0001), .in11(4'b0001), .in12(4'b0000),
    .in13(4'b0000), .in14(4'b0001), .in15(4'b0001), .out(multiplexer_1_out), .sel(bitselector_2_out));
  assign ALU_CONTROL_MUX_INPUT = {{2{1'b0}}, multiplexer_1_out};  // Bit_Extender bit_extender_4
  Multiplexer #(.width(5), .enable("false")) multiplexer_2 (
    .in0(RT), .in1(RD), .out(multiplexer_2_out), .sel(SIG_ALU_OP));
  // Probe on registerfile_1_p7
  // RegisterFile registerfile_1: pin names not known; wires that end beside it: WRITEBACK, CLK, SIG_RegWrite, multiplexer_2_out, RS, RT, registerfile_1_p7, B
  Decoder #(.select(4), .enable("false")) decoder_1 (
    .out0(decoder_1_out0), .out1(decoder_1_out1), .out2(decoder_1_out2), .out3(decoder_1_out3),
    .out4(decoder_1_out4), .out5(decoder_1_out5), .out6(decoder_1_out6), .out7(decoder_1_out7),
    .out8(decoder_1_out8), .out9(decoder_1_out9), .out10(SIG_MEM_READ), .out11(SIG_MemWrite),
    .out12(SIG_BEQ), .out13(SIG_BNE), .out14(SIG_JUMP), .out15(SIG_ADDI), .sel(bitselector_4_out));
  // Probe on B
  Multiplexer #(.width(32), .enable("false")) multiplexer_3 (
    .in0(B), .in1(SIGN_EXTENDED), .out(multiplexer_3_out), .sel(SIG_ALUSrc));
  // Probe on ALU_RESULT
  _32_Bit_ALU_V2_main main_1 (
    .A(registerfile_1_p7), .B(multiplexer_3_out), .OPCODE(ALU_CONTROL_MUX_INPUT), .C(ALU_RESULT),
    .Zero(main_1_zero));  // open: Carryout, Overflow
  ExactlyOne xor_1 (
    .out(SIG_ALU_OP), .in0(decoder_1_out0), .in1(decoder_1_out1), .in2(decoder_1_out2), .in3(decoder_1_out3),
    .in4(decoder_1_out4), .in5(decoder_1_out5), .in6(decoder_1_out6), .in7(decoder_1_out7),
    .in8(decoder_1_out8), .in9(decoder_1_out9));
  // Probe on ALU_RESULT
  BitSelector #(.width(32), .group(24)) bitselector_5 (.in(ALU_RESULT), .out(bitselector_5_out), .sel(1'b0));
  or or_1 (SIG_RegWrite, SIG_ADDI, SIG_ALU_OP, SIG_MEM_READ);
  and and_1 (and_1_out, SIG_BEQ, main_1_zero);
  not not_1 (not_1_out, main_1_zero);
  Multiplexer #(.width(32), .enable("false")) multiplexer_4 (
    .in0(PC_1), .in1(SIGN_EXTENDED), .out(multiplexer_4_out), .sel(or_2_out));
  or or_2 (or_2_out, and_1_out, and_2_out);
  or or_3 (SIG_ALUSrc, SIG_MEM_READ, SIG_MemWrite, SIG_ADDI);
  Multiplexer #(.width(32), .enable("false")) multiplexer_5 (
    .in0(multiplexer_4_out), .in1(JUMP_ADDRESS), .out(NEW_PC), .sel(SIG_JUMP));
  and and_2 (and_2_out, SIG_BNE, not_1_out);
  Multiplexer #(.width(32), .enable("false")) multiplexer_6 (
    .in0(ALU_RESULT), .in1(ram_1_data), .out(WRITEBACK), .sel(SIG_MEM_READ));
  RAM #(.addrWidth(24), .dataWidth(32), .bus("separate")) ram_1 (
    .addr(bitselector_5_out), .din(B), .data(ram_1_data), .str(SIG_MemWrite), .sel(1'b1), .clk(CLK),
    .ld(SIG_MEM_READ));  // open: clr

  // Other names for the same wires on the sheet: SIG_MEMTOREG = SIG_MEM_READ; SIG_RegDest = SIG_ALU_OP

  // Notes on the sheet:
  //   contents of rom_1 (hex, n*v repeats v):
  //   4001820 2a810000 2a820001 3e940002 8411018 4621820 3c051770 1ca3202a 3c060001 30c4000b 38000001
endmodule
