// Logisim project one-bit-adder.circ as structural Verilog: 1 circuit, main circuit 1-BIT-ADDER
module _1_BIT_ADDER (
  input  A,
  input  B,
  input  Carry,
  output Sum,
  output Carry_Out
);

  wire and_1_out, and_2_out, xor_1_out;

  xor xor_1 (xor_1_out, A, B);
  xor xor_2 (Sum, xor_1_out, Carry);
  and and_1 (and_1_out, Carry, A);
  and and_2 (and_2_out, A, B);
  or or_1 (Carry_Out, and_1_out, and_2_out);

  // Other names for the same wires on the sheet: C = Carry
endmodule
